// Logisim project Final draft design.circ as structural Verilog
module PC (
  input  [19:0] AC,
  input  [19:0] DR,
  input  [19:0] IR,
  input  FGO,
  input  FGI,
  input  R,
  input  E,
  input  [2:0] in_8,
  input  in_9,
  output [13:0] out_10
);

  wire or_1_out, pc_control_1_clear, pc_control_1_increment, pc_control_1_load;
  wire [13:0] adder_1_out, multiplexer_1_out;

  PC_control pc_control_1 (
    .IR(IR), .Load(pc_control_1_load), .Increment(pc_control_1_increment), .Clear(pc_control_1_clear),
    .SC(in_8), .R(R), .FGI(FGI), .FGO(FGO), .E(E), .AC(AC), .DR(DR));
  Multiplexer #(.width(14), .enable("false")) multiplexer_1 (
    .in0(IR[13:0]), .in1(adder_1_out), .out(multiplexer_1_out), .sel(pc_control_1_increment));
  Adder #(.width(14)) adder_1 (.a(14'h1), .b(out_10), .out(adder_1_out));  // open: cin, cout
  or or_1 (or_1_out, pc_control_1_increment, pc_control_1_load);
  Register #(.width(14)) register_1 (
    .D(multiplexer_1_out), .en(or_1_out), .Q(out_10), .clk(in_9), .clr(pc_control_1_clear));
endmodule

// PC Control
module PC_control (
  input  [19:0] IR,
  input  [2:0] SC,
  input  [19:0] AC,
  input  [19:0] DR,
  input  R,
  input  FGI,
  input  FGO,
  input  E,
  output Load,
  output Increment,
  output Clear
);

  wire and_3_out, and_4_out, and_5_out, and_6_out, and_7_out, and_8_out, and_9_out, and_10_out, and_11_out,
       and_12_out, and_13_out, decoder_1_out0, decoder_1_out1, decoder_1_out2, decoder_1_out3,
       decoder_1_out4, decoder_1_out5, decoder_1_out6, decoder_1_out7, decoder_2_out0, decoder_2_out1,
       decoder_2_out2, decoder_2_out3, decoder_2_out4, decoder_2_out5, decoder_2_out6, decoder_2_out7,
       decoder_2_out8, decoder_2_out9, decoder_2_out10, decoder_2_out11, decoder_2_out12, decoder_2_out13,
       decoder_2_out14, decoder_2_out15, or_1_out, or_2_out, p, r_t;

  Decoder #(.select(3)) decoder_1 (
    .out0(decoder_1_out0), .out1(decoder_1_out1), .out2(decoder_1_out2), .out3(decoder_1_out3),
    .out4(decoder_1_out4), .out5(decoder_1_out5), .out6(decoder_1_out6), .out7(decoder_1_out7), .sel(SC));  // open: en
  Decoder #(.select(4)) decoder_2 (
    .out0(decoder_2_out0), .out1(decoder_2_out1), .out2(decoder_2_out2), .out3(decoder_2_out3),
    .out4(decoder_2_out4), .out5(decoder_2_out5), .out6(decoder_2_out6), .out7(decoder_2_out7),
    .out8(decoder_2_out8), .out9(decoder_2_out9), .out10(decoder_2_out10), .out11(decoder_2_out11),
    .out12(decoder_2_out12), .out13(decoder_2_out13), .out14(decoder_2_out14), .out15(decoder_2_out15),
    .sel(IR[17:14]));  // open: en
  and and_1 (p, decoder_1_out3, IR[19], IR[18], decoder_2_out15);
  and and_2 (r_t, decoder_2_out0, decoder_1_out3, IR[19], IR[18]);
  or or_1 (or_1_out, AC[19], AC[18], AC[17], AC[16], AC[15], AC[14], AC[13], AC[12], AC[11], AC[10], AC[8], AC[7], AC[6], AC[5], AC[4], AC[3], AC[2], AC[1], AC[0], AC[9]);
  and and_3 (and_3_out, decoder_1_out5, decoder_2_out6);
  and and_4 (and_4_out, decoder_2_out7, decoder_1_out6);
  and and_5 (and_5_out, ~R, decoder_1_out1);  // AND_Gate
  and and_6 (and_6_out, R, decoder_1_out3);
  and and_7 (and_7_out, decoder_2_out8, ~or_2_out, decoder_1_out6);  // AND_Gate
  and and_8 (and_8_out, IR[6], r_t, ~AC[19]);  // AND_Gate
  and and_9 (and_9_out, IR[5], r_t, AC[19]);
  and and_10 (and_10_out, IR[4], r_t, or_1_out);
  and and_11 (and_11_out, IR[3], r_t, E);
  and and_12 (and_12_out, IR[11], p, FGI);
  and and_13 (and_13_out, IR[10], p, FGO);
  or or_2 (or_2_out, DR[19], DR[18], DR[17], DR[16], DR[15], DR[14], DR[13], DR[12], DR[11], DR[10], DR[8], DR[7], DR[6], DR[5], DR[4], DR[3], DR[2], DR[1], DR[0], DR[9]);
  or or_3 (Load, and_3_out, and_4_out);
  or or_4 (Increment, and_5_out, and_6_out, and_7_out, and_8_out, and_9_out, and_10_out, and_11_out, and_12_out, and_13_out);
  and and_14 (Clear, R, decoder_1_out2);

  // Notes on the sheet:
  //   3x8 decoder
  //   4x8 decoder
  //   D6T5
  //   D7T6
endmodule

module AC (
  input  [19:0] IR,
  input  [2:0] in_2,
  input  [19:0] ALU,
  input  in_4,
  output [19:0] out_5
);

  wire ac_control_1_clear, ac_control_1_increment, ac_control_1_load, or_1_out;
  wire [19:0] adder_1_out, multiplexer_1_out;

  AC_control ac_control_1 (
    .Clear(ac_control_1_clear), .Increment(ac_control_1_increment), .SC(in_2), .IR(IR),
    .Load(ac_control_1_load));
  Adder #(.width(20)) adder_1 (.a(20'h1), .b(out_5), .out(adder_1_out));  // open: cin, cout
  Multiplexer #(.width(20), .enable("false")) multiplexer_1 (
    .in0(ALU), .in1(adder_1_out), .out(multiplexer_1_out), .sel(ac_control_1_load));
  or or_1 (or_1_out, ac_control_1_load, ac_control_1_increment);
  Register #(.width(20)) register_1 (
    .D(multiplexer_1_out), .en(or_1_out), .Q(out_5), .clk(in_4), .clr(ac_control_1_clear));
endmodule

module AC_control (
  input  [19:0] IR,
  input  [2:0] SC,
  output Load,
  output Clear,
  output Increment
);

  wire and_1_out, and_2_out, and_3_out, and_4_out, and_5_out, and_6_out, and_7_out, and_8_out, and_9_out,
       decoder_1_out0, decoder_1_out1, decoder_1_out2, decoder_1_out3, decoder_1_out4, decoder_1_out5,
       decoder_1_out6, decoder_1_out7, decoder_2_out0, decoder_2_out1, decoder_2_out2, decoder_2_out3,
       decoder_2_out4, decoder_2_out5, decoder_2_out6, decoder_2_out7, decoder_2_out8, decoder_2_out9,
       decoder_2_out10, decoder_2_out11, decoder_2_out12, decoder_2_out13, decoder_2_out14, decoder_2_out15,
       p, r;

  Decoder #(.select(3)) decoder_1 (
    .out0(decoder_1_out0), .out1(decoder_1_out1), .out2(decoder_1_out2), .out3(decoder_1_out3),
    .out4(decoder_1_out4), .out5(decoder_1_out5), .out6(decoder_1_out6), .out7(decoder_1_out7), .sel(SC));  // open: en
  Decoder #(.select(4)) decoder_2 (
    .out0(decoder_2_out0), .out1(decoder_2_out1), .out2(decoder_2_out2), .out3(decoder_2_out3),
    .out4(decoder_2_out4), .out5(decoder_2_out5), .out6(decoder_2_out6), .out7(decoder_2_out7),
    .out8(decoder_2_out8), .out9(decoder_2_out9), .out10(decoder_2_out10), .out11(decoder_2_out11),
    .out12(decoder_2_out12), .out13(decoder_2_out13), .out14(decoder_2_out14), .out15(decoder_2_out15),
    .sel(IR[17:14]));  // open: en
  and and_1 (and_1_out, decoder_2_out0, decoder_1_out5);
  and and_2 (and_2_out, decoder_2_out1, decoder_1_out5);
  and and_3 (and_3_out, decoder_2_out2, decoder_1_out5);
  and and_4 (and_4_out, decoder_2_out3, decoder_1_out5);
  and and_5 (and_5_out, decoder_2_out4, decoder_1_out5);
  and and_6 (and_6_out, decoder_2_out9, decoder_1_out6);
  and and_7 (and_7_out, IR[9], r);
  and and_8 (and_8_out, IR[8], r);
  and and_9 (and_9_out, IR[11], p);
  and and_10 (p, decoder_1_out3, IR[19], IR[18], decoder_2_out15);
  and and_11 (r, decoder_2_out0, decoder_1_out3, IR[19], IR[18]);
  or or_1 (Load, and_1_out, and_2_out, and_3_out, and_4_out, and_5_out, and_6_out, and_7_out, and_8_out, and_9_out);
  and and_12 (Clear, IR[13], r);
  and and_13 (Increment, IR[7], p);

  // Notes on the sheet:
  //   3x8 decoder
  //   4x8 decoder
endmodule

module AR (
  input  [19:0] IR,
  input  in_2,
  input  in_3,
  output [13:0] Bus_OUT
);

  wire ar_control_1_clear, ar_control_1_increment, ar_control_1_load, clock_1_out, or_1_out;
  wire [13:0] adder_1_out, multiplexer_1_out;

  Clock clock_1 (.out(clock_1_out));
  AR_control ar_control_1 (
    .Load(ar_control_1_load), .Clear(ar_control_1_clear), .Increment(ar_control_1_increment), .R(in_3),
    .IR(IR), .Counter_Input(in_2));
  Multiplexer #(.width(14)) multiplexer_1 (
    .in0(IR[13:0]), .in1(adder_1_out), .out(multiplexer_1_out), .sel(ar_control_1_increment));  // open: en
  or or_1 (or_1_out, ar_control_1_increment, ar_control_1_load);
  Register #(.width(14)) register_1 (
    .D(multiplexer_1_out), .en(or_1_out), .Q(Bus_OUT), .clk(clock_1_out), .clr(ar_control_1_clear));
  Adder #(.width(14)) adder_1 (.a(14'h1), .b(Bus_OUT), .out(adder_1_out));  // open: cin, cout
endmodule

module AR_control (
  input  Counter_Input,
  input  [19:0] IR,
  input  R,
  output Load,
  output Clear,
  output Increment
);

  wire and_1_out, and_2_out, and_3_out, button_1_out, clock_1_out, decoder_1_out0, decoder_1_out1,
       decoder_1_out2, decoder_1_out3, decoder_1_out4, decoder_1_out5, decoder_1_out6, decoder_1_out7,
       decoder_2_out0, decoder_2_out1, decoder_2_out2, decoder_2_out3, decoder_2_out4, decoder_2_out5,
       decoder_2_out6, decoder_2_out7, decoder_2_out8, decoder_2_out9, decoder_2_out10, decoder_2_out11,
       decoder_2_out12, decoder_2_out13, decoder_2_out14, decoder_2_out15;
  wire [2:0] counter_1_q;

  Clock clock_1 (.out(clock_1_out));
  Counter #(.width(3), .max('h7)) counter_1 (
    .load(Counter_Input), .Q(counter_1_q), .clk(clock_1_out), .clr(button_1_out));  // open: D, count, carry
  Button button_1 (.out(button_1_out));
  Decoder #(.select(3)) decoder_1 (
    .out0(decoder_1_out0), .out1(decoder_1_out1), .out2(decoder_1_out2), .out3(decoder_1_out3),
    .out4(decoder_1_out4), .out5(decoder_1_out5), .out6(decoder_1_out6), .out7(decoder_1_out7),
    .sel(counter_1_q));  // open: en
  Decoder #(.select(4)) decoder_2 (
    .out0(decoder_2_out0), .out1(decoder_2_out1), .out2(decoder_2_out2), .out3(decoder_2_out3),
    .out4(decoder_2_out4), .out5(decoder_2_out5), .out6(decoder_2_out6), .out7(decoder_2_out7),
    .out8(decoder_2_out8), .out9(decoder_2_out9), .out10(decoder_2_out10), .out11(decoder_2_out11),
    .out12(decoder_2_out12), .out13(decoder_2_out13), .out14(decoder_2_out14), .out15(decoder_2_out15),
    .sel(IR[17:14]));  // open: en
  and and_1 (and_1_out, ~R, decoder_1_out0);  // AND_Gate
  and and_2 (and_2_out, ~decoder_2_out0, ~decoder_2_out15, decoder_1_out3, ~IR[18], ~IR[19]);  // AND_Gate
  and and_3 (and_3_out, ~R, decoder_1_out2);  // AND_Gate
  and and_4 (Clear, R, decoder_1_out1);
  and and_5 (Increment, decoder_2_out7, decoder_1_out5);
  or or_1 (Load, and_1_out, and_2_out, and_3_out);
endmodule

module DR (
  input  [19:0] in_1,
  input  [19:0] CBS_Mockup,
  input  in_3,
  input  in_4,
  output [19:0] out_5
);

  wire button_1_out, dr_control_1_increment, dr_control_1_load, or_1_out;
  wire [19:0] adder_1_out, multiplexer_1_out;

  DR_control dr_control_1 (.IR(in_1), .in_2(in_3), .Load(dr_control_1_load), .Increment(dr_control_1_increment));
  or or_1 (or_1_out, dr_control_1_load, dr_control_1_increment);
  Multiplexer #(.width(20), .enable("false")) multiplexer_1 (
    .in0(CBS_Mockup), .in1(adder_1_out), .out(multiplexer_1_out), .sel(dr_control_1_increment));
  Adder #(.width(20)) adder_1 (.a(20'h1), .b(out_5), .out(adder_1_out));  // open: cin, cout
  Button button_1 (.out(button_1_out));
  Register #(.width(20)) DR (.D(multiplexer_1_out), .en(or_1_out), .Q(out_5), .clk(in_4), .clr(button_1_out));
endmodule

// DR Control
module DR_control (
  input  [19:0] IR,
  input  in_2,
  output Load,
  output Increment
);

  wire and_1_out, and_2_out, and_3_out, and_4_out, button_1_out, clock_1_out, decoder_1_out0, decoder_1_out1,
       decoder_1_out2, decoder_1_out3, decoder_1_out4, decoder_1_out5, decoder_1_out6, decoder_1_out7,
       decoder_2_out0, decoder_2_out1, decoder_2_out2, decoder_2_out3, decoder_2_out4, decoder_2_out5,
       decoder_2_out6, decoder_2_out7, decoder_2_out8, decoder_2_out9, decoder_2_out10, decoder_2_out11,
       decoder_2_out12, decoder_2_out13, decoder_2_out14, decoder_2_out15;
  wire [2:0] counter_1_q;

  Counter #(.width(3), .max('h7)) counter_1 (
    .load(in_2), .Q(counter_1_q), .clk(clock_1_out), .clr(button_1_out));  // open: D, count, carry
  Clock clock_1 (.out(clock_1_out));
  Button button_1 (.out(button_1_out));
  Decoder #(.select(3)) decoder_1 (
    .out0(decoder_1_out0), .out1(decoder_1_out1), .out2(decoder_1_out2), .out3(decoder_1_out3),
    .out4(decoder_1_out4), .out5(decoder_1_out5), .out6(decoder_1_out6), .out7(decoder_1_out7),
    .sel(counter_1_q));  // open: en
  Decoder #(.select(4)) decoder_2 (
    .out0(decoder_2_out0), .out1(decoder_2_out1), .out2(decoder_2_out2), .out3(decoder_2_out3),
    .out4(decoder_2_out4), .out5(decoder_2_out5), .out6(decoder_2_out6), .out7(decoder_2_out7),
    .out8(decoder_2_out8), .out9(decoder_2_out9), .out10(decoder_2_out10), .out11(decoder_2_out11),
    .out12(decoder_2_out12), .out13(decoder_2_out13), .out14(decoder_2_out14), .out15(decoder_2_out15),
    .sel(IR[17:14]));  // open: en
  and and_1 (and_1_out, ~decoder_2_out0, ~decoder_2_out15, decoder_1_out3, ~IR[19], ~IR[18]);  // AND_Gate
  and and_2 (and_2_out, ~decoder_2_out0, ~decoder_2_out15, decoder_1_out4, ~IR[19], IR[18]);  // AND_Gate
  and and_3 (and_3_out, ~decoder_2_out0, ~decoder_2_out15, decoder_1_out3, IR[19], ~IR[18]);  // AND_Gate
  and and_4 (and_4_out, decoder_2_out9, decoder_1_out6);
  and and_5 (Increment, decoder_2_out8, decoder_1_out5);
  or or_1 (Load, and_1_out, and_2_out, and_3_out, and_4_out);
endmodule

module IR (
  input  in_1,
  input  in_2,
  input  [19:0] CBS_Mockup,
  input  in_4,
  output [19:0] out_5
);

  wire button_1_out, ir_control_1_load;

  IR_control ir_control_1 (.in_1(in_1), .R(in_2), .Load(ir_control_1_load));
  Button button_1 (.out(button_1_out));
  Register #(.width(20)) IR (.D(CBS_Mockup), .en(ir_control_1_load), .Q(out_5), .clk(in_4), .clr(button_1_out));
endmodule

module IR_control (
  input  in_1,
  input  R,
  output Load
);

  wire button_1_out, clock_1_out, decoder_1_out0, decoder_1_out1, decoder_1_out2, decoder_1_out3,
       decoder_1_out4, decoder_1_out5, decoder_1_out6, decoder_1_out7;
  wire [2:0] counter_1_q;

  Counter #(.width(3), .max('h7)) counter_1 (
    .load(in_1), .Q(counter_1_q), .clk(clock_1_out), .clr(button_1_out));  // open: D, count, carry
  Clock clock_1 (.out(clock_1_out));
  Button button_1 (.out(button_1_out));
  Decoder #(.select(3)) decoder_1 (
    .out0(decoder_1_out0), .out1(decoder_1_out1), .out2(decoder_1_out2), .out3(decoder_1_out3),
    .out4(decoder_1_out4), .out5(decoder_1_out5), .out6(decoder_1_out6), .out7(decoder_1_out7),
    .sel(counter_1_q));  // open: en
  and and_1 (Load, ~R, decoder_1_out1);  // AND_Gate
endmodule

// Tiiming decoder
module Timing_decoder (
  input  Counter_Input,
  output out_2,
  output out_3,
  output out_4,
  output out_5,
  output out_6,
  output out_7,
  output out_8,
  output out_9
);

  wire button_1_out, clock_1_out;
  wire [2:0] counter_1_q;

  Clock clock_1 (.out(clock_1_out));
  Counter #(.width(3), .max('h7)) counter_1 (
    .load(Counter_Input), .Q(counter_1_q), .clk(clock_1_out), .clr(button_1_out));  // open: D, count, carry
  Button button_1 (.out(button_1_out));
  Decoder #(.select(3)) decoder_1 (
    .out0(out_2), .out1(out_3), .out2(out_4), .out3(out_5), .out4(out_6), .out5(out_7), .out6(out_8),
    .out7(out_9), .sel(counter_1_q));  // open: en
endmodule

module Bus_Control (
  input  [19:0] IR,
  input  R,
  input  [2:0] in_3,
  output [2:0] out_4,
  output [2:0] out_5
);

  wire and_1_out, and_2_out, and_3_out, and_4_out, and_5_out, and_6_out, and_7_out, and_8_out, and_9_out,
       and_10_out, and_11_out, and_12_out, and_13_out, and_14_out, and_15_out, and_17_out, and_18_out,
       and_19_out, and_20_out, and_21_out, decoder_1_out0, decoder_1_out1, decoder_1_out2, decoder_1_out3,
       decoder_1_out4, decoder_1_out5, decoder_1_out6, decoder_1_out7, decoder_2_out0, decoder_2_out1,
       decoder_2_out2, decoder_2_out3, decoder_2_out4, decoder_2_out5, decoder_2_out6, decoder_2_out7,
       decoder_2_out8, decoder_2_out9, decoder_2_out10, decoder_2_out11, decoder_2_out12, decoder_2_out13,
       decoder_2_out14, decoder_2_out15, or_1_out, or_2_out, or_3_out, or_4_out, or_5_out, or_6_out, p;

  Decoder #(.select(3)) decoder_1 (
    .out0(decoder_1_out0), .out1(decoder_1_out1), .out2(decoder_1_out2), .out3(decoder_1_out3),
    .out4(decoder_1_out4), .out5(decoder_1_out5), .out6(decoder_1_out6), .out7(decoder_1_out7), .sel(in_3));  // open: en
  Decoder #(.select(4)) decoder_2 (
    .out0(decoder_2_out0), .out1(decoder_2_out1), .out2(decoder_2_out2), .out3(decoder_2_out3),
    .out4(decoder_2_out4), .out5(decoder_2_out5), .out6(decoder_2_out6), .out7(decoder_2_out7),
    .out8(decoder_2_out8), .out9(decoder_2_out9), .out10(decoder_2_out10), .out11(decoder_2_out11),
    .out12(decoder_2_out12), .out13(decoder_2_out13), .out14(decoder_2_out14), .out15(decoder_2_out15),
    .sel(IR[17:14]));  // open: en
  and and_1 (and_1_out, decoder_2_out6, decoder_1_out5);
  and and_2 (and_2_out, decoder_2_out7, decoder_1_out6);
  and and_3 (and_3_out, R, decoder_1_out0);
  and and_4 (and_4_out, R, decoder_1_out1);
  and and_5 (and_5_out, decoder_2_out7, decoder_1_out5);
  and and_6 (and_6_out, decoder_2_out4, decoder_1_out5);
  and and_7 (and_7_out, decoder_2_out8, decoder_1_out6);
  and and_8 (and_8_out, decoder_2_out9, decoder_1_out6);
  and and_9 (and_9_out, decoder_2_out5, decoder_1_out5);
  and and_10 (and_10_out, decoder_2_out9, decoder_1_out5);
  and and_11 (and_11_out, IR[12], p);
  and and_12 (and_12_out, ~R, decoder_1_out2);  // AND_Gate
  and and_13 (and_13_out, R, decoder_1_out2);
  and and_14 (and_14_out, decoder_2_out9, decoder_1_out6);
  and and_15 (and_15_out, ~R, decoder_1_out1);  // AND_Gate
  and and_16 (p, decoder_1_out3, IR[19], IR[18], decoder_2_out15);
  and and_17 (and_17_out, ~decoder_2_out0, ~decoder_2_out15, decoder_1_out3, IR[19], ~IR[18]);  // AND_Gate
  and and_18 (and_18_out, ~decoder_2_out0, ~decoder_2_out15, decoder_1_out3, ~IR[19], ~IR[18]);  // AND_Gate
  and and_19 (and_19_out, ~decoder_2_out0, ~decoder_2_out15, decoder_1_out3, ~IR[19], IR[18]);  // AND_Gate
  and and_20 (and_20_out, ~decoder_2_out0, ~decoder_2_out15, decoder_1_out4, ~IR[19], IR[18]);  // AND_Gate
  or or_1 (or_1_out, and_6_out, and_7_out, and_8_out);
  or or_2 (or_2_out, and_9_out, and_10_out, and_11_out);
  or or_3 (or_3_out, and_13_out, and_14_out);
  or or_4 (or_4_out, and_17_out, and_1_out, and_2_out);
  or or_5 (or_5_out, and_3_out, and_4_out, and_5_out);
  and and_21 (and_21_out, ~or_4_out, ~or_5_out, ~or_1_out, ~or_2_out, ~and_12_out, ~or_3_out, ~or_6_out);  // AND_Gate
  or or_6 (or_6_out, and_15_out, and_18_out, and_19_out, and_20_out);
  Priority_Encoder priority_encoder_1 (
    .in0(and_21_out), .in1(or_4_out), .in2(or_5_out), .in3(or_1_out), .in4(or_2_out), .in5(and_12_out),
    .in6(or_3_out), .in7(or_6_out), .out(out_5));  // open: en_in, gs, en_out
  Multiplexer #(.select(3), .width(3), .enable("false")) multiplexer_1 (
    .in0(3'b000), .in1(3'b001), .in2(3'b010), .in3(3'b011), .in4(3'b100), .in5(3'b101), .in6(3'b110),
    .in7(3'b111), .out(out_4), .sel(out_5));
endmodule
